// Logisim project 8bit register_TEST.circ as structural Verilog: 2 circuits, main circuit register
// REG
module register (
  input  [7:0] INPUT,
  input  LOAD,
  input  CLOCK,
  input  RESET,
  input  ENABLE,
  output [7:0] OUTPUT,
  output [7:0] STATUS
);

  wire [7:0] controlled_buffer_1_out;

  assign controlled_buffer_1_out = LOAD ? INPUT : 8'bz;  // Controlled_Buffer controlled_buffer_1
  assign controlled_buffer_1_out = ENABLE ? OUTPUT : 8'bz;  // Controlled_Buffer controlled_buffer_2
  Register #(.trigger("falling")) register_1 (
    .D(controlled_buffer_1_out), .en(LOAD), .Q(STATUS), .clk(CLOCK), .clr(RESET));
  assign OUTPUT = ENABLE ? STATUS : 8'bz;  // Controlled_Buffer controlled_buffer_3
endmodule

module TEST (
  input  enable,
  input  load,
  input  [7:0] LOAD_BUS,
  input  in_4,
  input  enable_2,
  input  load_2,
  input  enable_3,
  input  sub,
  input  enablr,
  output [7:0] BUS,
  output [7:0] out_11,
  output [7:0] out_12,
  output [7:0] out_13,
  output cout
);

  wire clock_1_out;

  assign BUS = enable_2 ? LOAD_BUS : 8'bz;  // Controlled_Buffer controlled_buffer_1
  alu alu_1 (.status(out_13), .OUTPUT(BUS), .SUB(sub), .ACC(out_11), .B_reg(out_12), .C_OUT(cout), .enable(enablr));
  register register_1 (
    .INPUT(BUS), .OUTPUT(BUS), .LOAD(load), .RESET(in_4), .STATUS(out_11), .ENABLE(enable),
    .CLOCK(clock_1_out));
  register register_2 (
    .INPUT(BUS), .OUTPUT(BUS), .LOAD(load_2), .RESET(in_4), .STATUS(out_12), .ENABLE(enable_3),
    .CLOCK(clock_1_out));
  Clock clock_1 (.out(clock_1_out));
endmodule
