// Logisim project ALUmodule.circ as structural Verilog: 1 circuit, main circuit alu
module alu (
  input  [7:0] ACC,
  input  enable,
  input  SUB,
  input  [7:0] B_reg,
  output [7:0] status,
  output [7:0] OUTPUT,
  output C_OUT
);

  wire [7:0] xor_8_out;

  xor xor_1 (xor_8_out[7], SUB, B_reg[7]);
  xor xor_2 (xor_8_out[5], SUB, B_reg[5]);
  xor xor_3 (xor_8_out[6], SUB, B_reg[6]);
  xor xor_4 (xor_8_out[3], SUB, B_reg[3]);
  xor xor_5 (xor_8_out[4], SUB, B_reg[4]);
  xor xor_6 (xor_8_out[2], SUB, B_reg[2]);
  xor xor_7 (xor_8_out[1], SUB, B_reg[1]);
  xor xor_8 (xor_8_out[0], SUB, B_reg[0]);
  Adder adder_1 (.a(ACC), .b(xor_8_out), .out(status), .cin(SUB), .cout(C_OUT));
  assign OUTPUT = enable ? status : 8'bz;  // Controlled_Buffer controlled_buffer_1
endmodule
