// Logisim project 8bit register.circ as structural Verilog: 1 circuit, main circuit register
module register (
  input  [7:0] INPUT,
  input  LOAD,
  input  CLOCK,
  input  RESET,
  input  ENABLE,
  output [7:0] OUTPUT,
  output [7:0] CONTENTS
);

  wire [7:0] controlled_buffer_1_out;

  assign controlled_buffer_1_out = LOAD ? INPUT : 8'bz;  // Controlled_Buffer controlled_buffer_1
  assign controlled_buffer_1_out = ENABLE ? OUTPUT : 8'bz;  // Controlled_Buffer controlled_buffer_2
  Register #(.trigger("falling")) register_1 (
    .D(controlled_buffer_1_out), .en(LOAD), .Q(CONTENTS), .clk(CLOCK), .clr(RESET));
  assign OUTPUT = ENABLE ? CONTENTS : 8'bz;  // Controlled_Buffer controlled_buffer_3
endmodule
