// Logisim project Register Test.circ as structural Verilog: 1 circuit, main circuit main
module main (
  input  [7:0] INPUT_TO_BUS,
  input  WRITE_TO_BUS,
  input  LOAD_A,
  input  OUT_A,
  input  LOAD_B,
  input  OUT_B,
  input  RESET,
  input  SUB_EN,
  input  ALU_OUT,
  output [7:0] BUS_CONTENT,
  output [7:0] REG_A_CONTENTS,
  output [7:0] REG_B_CONTENTS,
  output [7:0] ALU_CONTENTS,
  output C_OUT
);

  wire CLK_out;

  assign BUS_CONTENT = WRITE_TO_BUS ? INPUT_TO_BUS : 8'bz;  // Controlled_Buffer controlled_buffer_1
  Clock CLK (.out(CLK_out));
  register REG_A (
    .INPUT(BUS_CONTENT), .OUTPUT(BUS_CONTENT), .LOAD(LOAD_A), .RESET(RESET), .CONTENTS(REG_A_CONTENTS),
    .ENABLE(OUT_A), .CLOCK(CLK_out));
  register REG_B (
    .INPUT(BUS_CONTENT), .OUTPUT(BUS_CONTENT), .LOAD(LOAD_B), .RESET(RESET), .CONTENTS(REG_B_CONTENTS),
    .ENABLE(OUT_B), .CLOCK(CLK_out));
  alu alu_1 (
    .status(ALU_CONTENTS), .OUTPUT(BUS_CONTENT), .SUB(SUB_EN), .A_IN(REG_A_CONTENTS), .B_IN(REG_B_CONTENTS),
    .C_OUT(C_OUT), .ALU_OUT(ALU_OUT));
endmodule
