// Logisim project CPU Assembly 2025.circ as structural Verilog: 1 circuit, main circuit main
module main (
  input  [7:0] in_1,
  input  [7:0] in_2,
  input  in_3,
  input  in_4,
  input  in_5
);

  wire alu2025_1_p10;

  // Clock_Module_main main_1: pin names not known
  // ALU2025 alu2025_1: pin names not known; wires that end beside it: in_1, in_2, in_3, in_5, in_3, in_3, in_3, in_3, in_4, alu2025_1_p10
  // Probe on alu2025_1_p10
endmodule
