// Logisim project Clock Module.circ as structural Verilog: 1 circuit, main circuit main
module main (
  input  Clock_In,
  input  Halt,
  output Clock_Out
);

  wire not_1_out;

  and and_1 (Clock_Out, Clock_In, not_1_out);
  not not_1 (not_1_out, Halt);
endmodule
