// Logisim project Pos Edge Trigger Detection.circ as structural Verilog: 1 circuit, main circuit main
module main (
);

  wire and_1_out, and_2_out, nor_1_out, nor_2_out, undriven, undriven_2, undriven_3;

  and and_1 (and_1_out, nor_1_out, undriven, undriven_3);
  and and_2 (and_2_out, undriven_3, undriven_2, nor_2_out);
  nor nor_1 (nor_1_out, and_1_out, nor_2_out);
  nor nor_2 (nor_2_out, nor_1_out, and_2_out);
endmodule
