// Logisim project 4bit counter 74 based.circ as structural Verilog: 1 circuit, main circuit main
module main (
  input  nCLR,
  input  nload,
  input  ENT,
  input  ENP,
  input  clk,
  input  A,
  input  B,
  input  C,
  input  D,
  output RCO,
  output QA,
  output QB,
  output QC,
  output QD
);

  wire and_1_out, and_2_out, and_3_out, and_4_out, buffer_1_out, buffer_2_out, main_1_q2, main_2_q2,
       main_3_q2, main_4_q2, nand_1_out, nand_2_out, not_1_out, not_2_out, not_3_out, not_4_out, not_5_out,
       not_6_out, not_7_out;

  buf buffer_1 (buffer_1_out, nCLR);
  nand nand_1 (nand_1_out, ENP, ENT, nload);
  not not_1 (not_1_out, nload);
  buf buffer_2 (buffer_2_out, not_1_out);
  not not_2 (not_2_out, nand_1_out);
  nand nand_2 (nand_2_out, main_2_q2, main_3_q2);
  not not_3 (not_3_out, nand_2_out);
  not not_4 (not_4_out, nand_1_out);
  not not_5 (not_5_out, clk);
  and and_1 (and_1_out, main_1_q2, not_6_out);
  not not_6 (not_6_out, nand_1_out);
  and and_2 (and_2_out, main_2_q2, main_1_q2, not_7_out);
  not not_7 (not_7_out, nand_1_out);
  and and_3 (and_3_out, main_1_q2, and_4_out);
  and and_4 (and_4_out, not_3_out, not_4_out);
  ff_main main_1 (
    .nR(buffer_1_out), .TE(not_2_out), .nclk(not_5_out), .D(A), .Load(buffer_2_out), .Q1(QA), .Q2(main_1_q2));
  ff_main main_2 (
    .nR(buffer_1_out), .TE(and_1_out), .nclk(not_5_out), .D(B), .Load(buffer_2_out), .Q1(QB), .Q2(main_2_q2));
  ff_main main_3 (
    .nR(buffer_1_out), .TE(and_2_out), .nclk(not_5_out), .D(C), .Load(buffer_2_out), .Q1(QC), .Q2(main_3_q2));
  ff_main main_4 (
    .nR(buffer_1_out), .TE(and_3_out), .nclk(not_5_out), .D(D), .Load(buffer_2_out), .Q1(QD), .Q2(main_4_q2));
  and and_5 (RCO, buffer_1_out, ENT, main_1_q2, main_2_q2, main_3_q2, main_4_q2);
endmodule
