// Logisim project 4bit reg 74 based.circ as structural Verilog: 1 circuit, main circuit main
module main (
  input  M,
  input  N,
  input  _1D,
  input  G1B,
  input  G2B,
  input  _2D,
  input  CLK,
  input  _3D,
  input  _4D,
  input  CLR,
  output _1Q,
  output _2Q,
  output _3Q,
  output _4Q
);

  wire and_1_out, and_2_out, and_3_out, and_4_out, and_5_out, and_6_out, and_7_out, and_8_out, and_9_out,
       and_10_out, d_ff_1_q, d_ff_1_qn, d_ff_2_q, d_ff_2_qn, d_ff_3_q, d_ff_3_qn, d_ff_4_q, d_ff_4_qn,
       not_1_out, not_2_out, not_3_out, not_4_out, not_5_out, not_6_out, not_7_out, not_8_out, not_9_out,
       or_1_out, or_2_out, or_3_out, or_4_out;

  Pull_Resistor #(.pull(1)) pull_resistor_1 (.node(G1B));
  Pull_Resistor #(.pull(1)) pull_resistor_2 (.node(G2B));
  not not_1 (not_1_out, M);
  and and_1 (and_1_out, not_1_out, not_2_out);
  not not_2 (not_2_out, N);
  not not_3 (not_3_out, G1B);
  and and_2 (and_2_out, not_3_out, not_4_out);
  not not_4 (not_4_out, G2B);
  not not_5 (not_5_out, and_2_out);
  and and_3 (and_3_out, d_ff_1_q, not_5_out);
  and and_4 (and_4_out, _1D, and_2_out);
  and and_5 (and_5_out, d_ff_2_q, not_5_out);
  and and_6 (and_6_out, _2D, and_2_out);
  and and_7 (and_7_out, d_ff_3_q, not_5_out);
  and and_8 (and_8_out, _3D, and_2_out);
  and and_9 (and_9_out, d_ff_4_q, not_5_out);
  and and_10 (and_10_out, _4D, and_2_out);
  or or_1 (or_1_out, and_3_out, and_4_out);
  or or_2 (or_2_out, and_5_out, and_6_out);
  or or_3 (or_3_out, and_7_out, and_8_out);
  or or_4 (or_4_out, and_9_out, and_10_out);
  D_Flip_Flop d_ff_1 (.clk(CLK), .D(or_1_out), .Q(d_ff_1_q), .Qn(d_ff_1_qn), .en(1'b1), .reset(CLR));  // open: preset
  not not_6 (not_6_out, d_ff_1_qn);
  D_Flip_Flop d_ff_2 (.clk(CLK), .D(or_2_out), .Q(d_ff_2_q), .Qn(d_ff_2_qn), .en(1'b1), .reset(CLR));  // open: preset
  not not_7 (not_7_out, d_ff_2_qn);
  D_Flip_Flop d_ff_3 (.clk(CLK), .D(or_3_out), .Q(d_ff_3_q), .Qn(d_ff_3_qn), .en(1'b1), .reset(CLR));  // open: preset
  not not_8 (not_8_out, d_ff_3_qn);
  D_Flip_Flop d_ff_4 (.clk(CLK), .D(or_4_out), .Q(d_ff_4_q), .Qn(d_ff_4_qn), .en(1'b1), .reset(CLR));  // open: preset
  not not_9 (not_9_out, d_ff_4_qn);
  assign _1Q = and_1_out ? not_6_out : 1'bz;  // Controlled_Buffer controlled_buffer_1
  assign _2Q = and_1_out ? not_7_out : 1'bz;  // Controlled_Buffer controlled_buffer_2
  assign _3Q = and_1_out ? not_8_out : 1'bz;  // Controlled_Buffer controlled_buffer_3
  assign _4Q = and_1_out ? not_9_out : 1'bz;  // Controlled_Buffer controlled_buffer_4

  // Notes on the sheet:
  //   G2B: pull=up
  //   G1B: pull=up
endmodule
