// Logisim project 8bit reg module 74 based.circ as structural Verilog: 1 circuit, main circuit main
module main (
  input  [7:0] datain,
  input  loadn,
  input  clk,
  input  rst,
  input  oe,
  output [7:0] internal_content,
  output [7:0] bus
);

  wire not_1_out, not_2_out;
  wire [7:0] controlled_buffer_1_out;

  assign controlled_buffer_1_out = not_1_out ? datain : 8'bz;  // Controlled_Buffer controlled_buffer_1
  not not_1 (not_1_out, loadn);
  Pull_Resistor #(.pull(1)) pull_resistor_1 (.node(loadn));
  assign controlled_buffer_1_out = not_2_out ? bus : 8'bz;  // Controlled_Buffer controlled_buffer_2
  _4bit_reg_74_based_main main_1 (
    .M(1'b0), .N(1'b0), ._1D(controlled_buffer_1_out[0]), .G1B(loadn), .G2B(loadn),
    ._2D(controlled_buffer_1_out[1]), .CLK(clk), ._3D(controlled_buffer_1_out[2]),
    ._4D(controlled_buffer_1_out[3]), .CLR(rst), ._1Q(internal_content[0]), ._2Q(internal_content[1]),
    ._3Q(internal_content[2]), ._4Q(internal_content[3]));
  _4bit_reg_74_based_main main_2 (
    .M(1'b0), .N(1'b0), ._1D(controlled_buffer_1_out[4]), .G1B(loadn), .G2B(loadn),
    ._2D(controlled_buffer_1_out[5]), .CLK(clk), ._3D(controlled_buffer_1_out[6]),
    ._4D(controlled_buffer_1_out[7]), .CLR(rst), ._1Q(internal_content[4]), ._2Q(internal_content[5]),
    ._3Q(internal_content[6]), ._4Q(internal_content[7]));
  not not_2 (not_2_out, oe);
  assign bus = oe ? internal_content : 8'bz;  // Controlled_Buffer controlled_buffer_3

  // Notes on the sheet:
  //   loadn: pull=up
endmodule
