// Logisim project 8bit reg module logi based.circ as structural Verilog: 1 circuit, main circuit register
module register (
  input  [7:0] datain,
  input  load,
  input  clk,
  input  rst,
  input  oe,
  output [7:0] bus,
  output [7:0] contents
);

  wire [7:0] controlled_buffer_1_out;

  assign controlled_buffer_1_out = load ? datain : 8'bz;  // Controlled_Buffer controlled_buffer_1
  assign controlled_buffer_1_out = oe ? bus : 8'bz;  // Controlled_Buffer controlled_buffer_2
  Register #(.trigger("falling")) register_1 (
    .D(controlled_buffer_1_out), .en(load), .Q(contents), .clk(clk), .clr(rst));
  assign bus = oe ? contents : 8'bz;  // Controlled_Buffer controlled_buffer_3
endmodule
