// Logisim project ALU module.circ as structural Verilog: 9 circuits, main circuit ALU2025
module ALU2025 (
  input  [7:0] B,
  input  [7:0] A,
  input  Bus_Enable,
  input  Sub_Cin,
  input  Add,
  input  Mul,
  input  XOR,
  input  AND,
  input  OR,
  input  rst,
  input  Clk,
  input  Flag_In,
  output Cout,
  output [7:0] contents,
  output [7:0] OUTPUT,
  output [7:0] Flag_Status
);

  wire [1:1] nor_1_out;
  wire [7:0] add_sub_1_sum, and_1_y, mul_1_mout, or_1_y, xor_1_y;

  ADD___SUB add_sub_1 (.Subtraction(Sub_Cin), .A(A), .B(B), .Sum(add_sub_1_sum), .Cout(Cout));
  MUL mul_1 (.A(A), .B(B), .Mout(mul_1_mout));
  XOR xor_1 (.A(A), .B(B), .Y(xor_1_y));
  AND and_1 (.A(A), .B(B), .Y(and_1_y));
  OR or_1 (.A(A), .B(B), .Y(or_1_y));
  // Probe on add_sub_1_sum
  // Probe on mul_1_mout
  // Probe on xor_1_y
  // Probe on and_1_y
  // Probe on or_1_y
  assign contents = Add ? add_sub_1_sum : 8'bz;  // Controlled_Buffer controlled_buffer_1
  assign contents = Mul ? mul_1_mout : 8'bz;  // Controlled_Buffer controlled_buffer_2
  assign contents = XOR ? xor_1_y : 8'bz;  // Controlled_Buffer controlled_buffer_3
  assign contents = AND ? and_1_y : 8'bz;  // Controlled_Buffer controlled_buffer_4
  assign contents = OR ? or_1_y : 8'bz;  // Controlled_Buffer controlled_buffer_5
  nor nor_1 (nor_1_out[1], contents[0], contents[1], contents[2], contents[3], contents[4], contents[5], contents[6], contents[7]);
  assign OUTPUT = Bus_Enable ? contents : 8'bz;  // Controlled_Buffer controlled_buffer_6
  _8bit_reg_module_74_based_main main_1 (
    .internal_content(Flag_Status), .datain({{6{1'b0}}, nor_1_out[1], Cout}), .loadn(Flag_In), .clk(Clk),
    .rst(rst), .oe(1'b1));  // open: bus

  // Notes on the sheet:
  //   ALU
  //   AV-CORE-V3.0
  //   Carry operation: Multiplixer
  //   to choose carry to be 1 or 0 or current Carry Flag
endmodule

module ADD___SUB (
  input  Subtraction,
  input  [7:0] A,
  input  [7:0] B,
  output [7:0] Sum,
  output Cout
);

  wire [7:0] xor_1_out;

  xor xor_1 (xor_1_out[0], Subtraction, B[0]);
  xor xor_2 (xor_1_out[1], Subtraction, B[1]);
  xor xor_3 (xor_1_out[2], Subtraction, B[2]);
  xor xor_4 (xor_1_out[3], Subtraction, B[3]);
  xor xor_5 (xor_1_out[4], Subtraction, B[4]);
  xor xor_6 (xor_1_out[5], Subtraction, B[5]);
  xor xor_7 (xor_1_out[6], Subtraction, B[6]);
  xor xor_8 (xor_1_out[7], Subtraction, B[7]);
  _8_BIT_FA u_8_bit_fa_1 (.S(Sum), .A(A), .B(xor_1_out), .Cin(Subtraction), .Cout(Cout));
endmodule

module MUL (
  input  [7:0] A,
  input  [7:0] B,
  output [7:0] Mout
);

  wire [2:0] and_16_out;
  wire [3:0] and_5_out, and_9_out, and_13_out, n4_bit_fa_2_cout;
  wire [3:1] n4_bit_fa_3_s;
  wire [3:3] n4_bit_fa_3_cout;

  and and_1 (and_5_out[3], B[3], A[3]);
  and and_2 (and_5_out[1], B[3], A[1]);
  and and_3 (and_5_out[2], B[3], A[2]);
  and and_4 (and_9_out[3], B[2], A[3]);
  and and_5 (and_5_out[0], B[3], A[0]);
  and and_6 (and_9_out[2], B[2], A[2]);
  and and_7 (and_9_out[1], B[2], A[1]);
  _4_Bit_FA u_4_bit_fa_1 (.S(Mout[6:3]), .A(n4_bit_fa_2_cout), .B(and_5_out), .Cin(1'b0), .Cout(Mout[7]));
  and and_8 (and_13_out[3], B[1], A[3]);
  and and_9 (and_9_out[0], B[2], A[0]);
  and and_10 (and_13_out[1], B[1], A[1]);
  and and_11 (and_13_out[2], B[1], A[2]);
  _4_Bit_FA u_4_bit_fa_2 (
    .S({n4_bit_fa_2_cout[2:0], Mout[2]}), .A({n4_bit_fa_3_cout[3], n4_bit_fa_3_s}), .B(and_9_out),
    .Cin(1'b0), .Cout(n4_bit_fa_2_cout[3]));
  and and_12 (and_16_out[2], B[0], A[3]);
  and and_13 (and_13_out[0], B[1], A[0]);
  and and_14 (Mout[0], B[0], A[0]);
  and and_15 (and_16_out[1], B[0], A[2]);
  and and_16 (and_16_out[0], B[0], A[1]);
  _4_Bit_FA u_4_bit_fa_3 (
    .S({n4_bit_fa_3_s, Mout[1]}), .A({1'b0, and_16_out}), .B(and_13_out), .Cin(1'b0),
    .Cout(n4_bit_fa_3_cout[3]));
endmodule

module XOR (
  input  [7:0] A,
  input  [7:0] B,
  output [7:0] Y
);

  xor xor_1 (Y[0], B[0], A[0]);
  xor xor_2 (Y[1], B[1], A[1]);
  xor xor_3 (Y[2], B[2], A[2]);
  xor xor_4 (Y[3], B[3], A[3]);
  xor xor_5 (Y[4], B[4], A[4]);
  xor xor_6 (Y[5], B[5], A[5]);
  xor xor_7 (Y[6], B[6], A[6]);
  xor xor_8 (Y[7], B[7], A[7]);
endmodule

module AND (
  input  [7:0] A,
  input  [7:0] B,
  output [7:0] Y
);

  and and_1 (Y[0], B[0], A[0]);
  and and_2 (Y[1], B[1], A[1]);
  and and_3 (Y[2], B[2], A[2]);
  and and_4 (Y[3], B[3], A[3]);
  and and_5 (Y[4], B[4], A[4]);
  and and_6 (Y[5], B[5], A[5]);
  and and_7 (Y[6], B[6], A[6]);
  and and_8 (Y[7], B[7], A[7]);
endmodule

module OR (
  input  [7:0] A,
  input  [7:0] B,
  output [7:0] Y
);

  or or_1 (Y[0], B[0], A[0]);
  or or_2 (Y[1], B[1], A[1]);
  or or_3 (Y[2], B[2], A[2]);
  or or_4 (Y[3], B[3], A[3]);
  or or_5 (Y[4], B[4], A[4]);
  or or_6 (Y[5], B[5], A[5]);
  or or_7 (Y[6], B[6], A[6]);
  or or_8 (Y[7], B[7], A[7]);
endmodule

module _8_BIT_FA (
  input  [7:0] A,
  input  [7:0] B,
  input  Cin,
  output [7:0] S,
  output Cout
);

  wire fa_1_cout, fa_2_cout, fa_3_cout, fa_4_cout, fa_5_cout, fa_6_cout, fa_7_cout;

  FA fa_1 (.A(B[0]), .B(A[0]), .Cin(Cin), .S(S[0]), .Cout(fa_1_cout));
  FA fa_2 (.A(B[1]), .B(A[1]), .Cin(fa_1_cout), .S(S[1]), .Cout(fa_2_cout));
  FA fa_3 (.A(B[2]), .B(A[2]), .Cin(fa_2_cout), .S(S[2]), .Cout(fa_3_cout));
  FA fa_4 (.A(B[3]), .B(A[3]), .Cin(fa_3_cout), .S(S[3]), .Cout(fa_4_cout));
  FA fa_5 (.A(B[4]), .B(A[4]), .Cin(fa_4_cout), .S(S[4]), .Cout(fa_5_cout));
  FA fa_6 (.A(B[5]), .B(A[5]), .Cin(fa_5_cout), .S(S[5]), .Cout(fa_6_cout));
  FA fa_7 (.A(B[6]), .B(A[6]), .Cin(fa_6_cout), .S(S[6]), .Cout(fa_7_cout));
  FA fa_8 (.A(B[7]), .B(A[7]), .Cin(fa_7_cout), .S(S[7]), .Cout(Cout));
endmodule

module _4_Bit_FA (
  input  [3:0] A,
  input  [3:0] B,
  input  Cin,
  output [3:0] S,
  output Cout
);

  wire fa_1_cout, fa_2_cout, fa_3_cout;

  FA fa_1 (.A(A[0]), .B(B[0]), .Cin(Cin), .S(S[0]), .Cout(fa_1_cout));
  FA fa_2 (.A(A[1]), .B(B[1]), .Cin(fa_1_cout), .S(S[1]), .Cout(fa_2_cout));
  FA fa_3 (.A(A[2]), .B(B[2]), .Cin(fa_2_cout), .S(S[2]), .Cout(fa_3_cout));
  FA fa_4 (.A(A[3]), .B(B[3]), .Cin(fa_3_cout), .S(S[3]), .Cout(Cout));
endmodule

module FA (
  input  A,
  input  B,
  input  Cin,
  output S,
  output Cout
);

  wire and_1_out, and_2_out, xor_1_out;

  and and_1 (and_1_out, A, B);
  xor xor_1 (xor_1_out, A, B);
  and and_2 (and_2_out, xor_1_out, Cin);
  xor xor_2 (S, xor_1_out, Cin);
  or or_1 (Cout, and_2_out, and_1_out);
endmodule
