// Logisim project CPU Assembly 2026.circ as structural Verilog: 1 circuit, main circuit main
// Reset
module main (
  input  CE,
  input  CO,
  input  JE,
  input  AI,
  input  AO,
  input  [7:0] in_6,
  input  in_7,
  input  SU,
  input  MI,
  input  AD,
  input  SO,
  input  RI,
  input  BI,
  input  RO,
  input  BO,
  input  II,
  input  OI,
  input  IO,
  input  MN,
  input  in_20,
  output OV
);

  wire AD_t, AI_t, alu2025_1_cout, AO_t, BI_t, BO_t, CE_t, clock, clock_1_out, CO_t, HLT, II_t, IO_t, JE_t,
       main_6_sign_s0, MI_t, MN_t, multiplexer_1_out, multiplexer_2_out, multiplexer_3_out,
       multiplexer_4_out, multiplexer_5_out, multiplexer_6_out, multiplexer_7_out, multiplexer_8_out,
       multiplexer_9_out, multiplexer_10_out, multiplexer_11_out, multiplexer_12_out, multiplexer_13_out,
       multiplexer_14_out, multiplexer_15_out, multiplexer_16_out, multiplexer_17_out, not_1_out, not_2_out,
       not_3_out, not_4_out, not_5_out, OI_t, reset, RI_t, RO_t, SO_t, SU_t;
  wire [2:0] main_3_step_line;
  wire [3:0] main_2_lsb_st, main_2_msb_st, main_4__4bit_data_out, main_6_bottom_s1, main_6_bottom_s2,
       main_6_bottom_s3, main_6_top_s1, main_6_top_s2, main_6_top_s3;
  wire [6:0] main_3_status;
  wire [7:0] alu2025_1_contents, main_1_bus, main_1_contents, main_4_contents, main_5_contents,
       main_7_internal_content, main_8_internal_content;
  wire [23:0] main_6_status;

  Multiplexer #(.enable("false")) multiplexer_1 (.in0(MI), .in1(MI_t), .out(multiplexer_1_out), .sel(in_20));
  Multiplexer #(.enable("false")) multiplexer_2 (.in0(RI), .in1(RI_t), .out(multiplexer_2_out), .sel(in_20));
  Multiplexer #(.enable("false")) multiplexer_3 (.in0(RO), .in1(RO_t), .out(multiplexer_3_out), .sel(in_20));
  Multiplexer #(.enable("false")) multiplexer_4 (.in0(II), .in1(II_t), .out(multiplexer_4_out), .sel(in_20));
  Multiplexer #(.enable("false")) multiplexer_5 (.in0(IO), .in1(IO_t), .out(multiplexer_5_out), .sel(in_20));
  not not_1 (not_1_out, multiplexer_4_out);
  // Probe on main_1_bus
  // Probe on main_4_contents
  // Probe on main_1_contents
  ram_module_without_MAR_main main_1 (
    .data_in(main_1_bus), .oe(multiplexer_3_out), .write(multiplexer_2_out), .contents(main_1_contents),
    .bus(main_1_bus), .add_in(main_4__4bit_data_out), .clk(clock));  // open: clr
  // Probe on main_2_msb_st
  instruction_register_module_main main_2 (
    .Datain(main_1_bus), .loadin(not_1_out), .clk(clock), .rst(reset), .oen(multiplexer_5_out),
    .Bus(main_1_bus), .MSB_ST(main_2_msb_st), .LSB_ST(main_2_lsb_st), .Instr_nibble(main_3_status[6:3]));
  fetch_cycle_tracker_main main_3 (.nclk(clock), .STATUS(main_3_status[2:0]), .STEP_LINE(main_3_step_line));
  // Probe on main_1_bus
  assign main_1_bus = in_7 ? in_6 : 8'bz;  // Controlled_Buffer controlled_buffer_1
  MAR_module_main main_4 (
    .load_in(multiplexer_1_out), .rst(reset), .clk(clock), .bus_datain(main_1_bus),
    ._4bit_data_out(main_4__4bit_data_out), .contents(main_4_contents));
  // Probe on main_2_lsb_st
  // Probe on main_3_status[6:3]
  // Probe on main_3_status[2:0]
  // Probe on main_3_step_line
  Pull_Resistor pull_resistor_1 (.node(main_1_bus));
  ROM #(.addrWidth(7), .dataWidth(16)) rom_1 (
    .addr(main_3_status),
    .data({MN_t, JE_t, CO_t, CE_t, OI_t, BI_t, SU_t, SO_t, AO_t, AI_t, II_t, IO_t, RO_t, RI_t, MI_t, HLT}),
    .sel(1'b1));
  PC_module_logi_based_main main_5 (
    .data_in(main_1_bus), .oen(multiplexer_7_out), .rst(reset), .Overflow(OV), .bus(main_1_bus),
    .contents(main_5_contents), .counten(multiplexer_6_out), .nload(not_2_out), .clk(clock));
  // Probe on main_8_internal_content
  display_main main_6 (
    .loadn(not_5_out), .bus(main_1_bus), .rst(reset), .clk(clock), .TOP_S3(main_6_top_s3),
    .BOTTOM_S3(main_6_bottom_s3), .TOP_S2(main_6_top_s2), .BOTTOM_S2(main_6_bottom_s2),
    .MODE(multiplexer_17_out), .TOP_S1(main_6_top_s1), .BOTTOM_S1(main_6_bottom_s1),
    .SIGN_S0(main_6_sign_s0), .STATUS(main_6_status));  // open: SEG3, SEG2, SEG1
  _7_Segment_Display u_7_segment_display_1 (
    .g(main_6_top_s1[3]), .f(main_6_top_s1[2]), .a(main_6_top_s1[1]), .b(main_6_top_s1[0]),
    .e(main_6_bottom_s1[3]), .d(main_6_bottom_s1[2]), .c(main_6_bottom_s1[1]), .dp(main_6_bottom_s1[0]));
  _7_Segment_Display u_7_segment_display_2 (.g(main_6_sign_s0));  // open: f, a, b, e, d, c, dp
  Clock clock_1 (.out(clock_1_out));
  // Probe on main_5_contents
  _8bit_reg_module_74_based_main main_7 (
    .internal_content(main_7_internal_content), .datain(main_1_bus), .loadn(not_3_out), .clk(clock),
    .rst(reset), .oe(multiplexer_10_out), .bus(main_1_bus));
  // Probe on main_7_internal_content
  // Probe on alu2025_1_contents
  ALU2025 alu2025_1 (
    .Cout(alu2025_1_cout), .OUTPUT(main_1_bus), .B(main_8_internal_content), .A(main_7_internal_content),
    .Sub_Cin(multiplexer_11_out), .Add(multiplexer_12_out), .Mul(1'b0), .XOR(1'b0), .AND(1'b0), .OR(1'b0),
    .Bus_Enable(multiplexer_13_out), .contents(alu2025_1_contents));
  _8bit_reg_module_74_based_main main_8 (
    .internal_content(main_8_internal_content), .datain(main_1_bus), .loadn(not_4_out), .clk(clock),
    .rst(reset), .oe(multiplexer_15_out), .bus(main_1_bus));
  // Probe on main_6_status
  _7_Segment_Display u_7_segment_display_3 (
    .g(main_6_top_s2[3]), .f(main_6_top_s2[2]), .a(main_6_top_s2[1]), .b(main_6_top_s2[0]),
    .e(main_6_bottom_s2[3]), .d(main_6_bottom_s2[2]), .c(main_6_bottom_s2[1]), .dp(main_6_bottom_s2[0]));
  _7_Segment_Display u_7_segment_display_4 (
    .g(main_6_top_s3[3]), .f(main_6_top_s3[2]), .a(main_6_top_s3[1]), .b(main_6_top_s3[0]),
    .e(main_6_bottom_s3[3]), .d(main_6_bottom_s3[2]), .c(main_6_bottom_s3[1]), .dp(main_6_bottom_s3[0]));
  Clock_Module_main main_9 (.Clock_In(clock_1_out), .Halt(HLT), .Clock_Out(clock));
  Button u_reset (.out(reset));
  Pull_Resistor #(.pull(1)) pull_resistor_2 (.node(in_20));
  not not_2 (not_2_out, multiplexer_8_out);
  not not_3 (not_3_out, multiplexer_9_out);
  // Probe on alu2025_1_cout
  not not_4 (not_4_out, multiplexer_14_out);
  not not_5 (not_5_out, multiplexer_16_out);
  Multiplexer #(.enable("false")) multiplexer_6 (.in0(CE), .in1(CE_t), .out(multiplexer_6_out), .sel(in_20));
  Multiplexer #(.enable("false")) multiplexer_7 (.in0(CO), .in1(CO_t), .out(multiplexer_7_out), .sel(in_20));
  Multiplexer #(.enable("false")) multiplexer_8 (.in0(JE), .in1(JE_t), .out(multiplexer_8_out), .sel(in_20));
  Multiplexer #(.enable("false")) multiplexer_9 (.in0(AI), .in1(AI_t), .out(multiplexer_9_out), .sel(in_20));
  Multiplexer #(.enable("false")) multiplexer_10 (.in0(AO), .in1(AO_t), .out(multiplexer_10_out), .sel(in_20));
  Multiplexer #(.enable("false")) multiplexer_11 (.in0(SU), .in1(SU_t), .out(multiplexer_11_out), .sel(in_20));
  Multiplexer #(.enable("false")) multiplexer_12 (.in0(AD), .in1(AD_t), .out(multiplexer_12_out), .sel(in_20));
  Multiplexer #(.enable("false")) multiplexer_13 (.in0(SO), .in1(SO_t), .out(multiplexer_13_out), .sel(in_20));
  Multiplexer #(.enable("false")) multiplexer_14 (.in0(BI), .in1(BI_t), .out(multiplexer_14_out), .sel(in_20));
  Multiplexer #(.enable("false")) multiplexer_15 (.in0(BO), .in1(BO_t), .out(multiplexer_15_out), .sel(in_20));
  Multiplexer #(.enable("false")) multiplexer_16 (.in0(OI), .in1(OI_t), .out(multiplexer_16_out), .sel(in_20));
  Multiplexer #(.enable("false")) multiplexer_17 (.in0(MN), .in1(MN_t), .out(multiplexer_17_out), .sel(in_20));
  Pull_Resistor pull_resistor_3 (.node(BO_t));
  Pull_Resistor #(.pull(1)) pull_resistor_4 (.node(AD_t));
  Pull_Resistor pull_resistor_5 (.node(MN_t));

  // Other names for the same wires on the sheet: AUTO = in_20

  // Notes on the sheet:
  //   in_20: pull=up
  //   contents of rom_1 (hex, n*v repeats v):
  //   2002 1028 6*0 2002 1028 12 48 4*0 2002 1028 12 408 140 0 0 0 2002 1028 6*0 2002 1028 6*0 2002 1028
  //   6*0 2002 1028 6*0 2002 1028 6*0 2002 1028 6*0 2002 1028 6*0 2002 1028 6*0 2002 1028 6*0 2002 1028
  //   6*0 2002 1028 6*0 2002 1028 880 5*0 2002 1028 1
  //   A
  //   B
  //   Make all control signals active High
endmodule
