// Logisim project MAR module.circ as structural Verilog: 1 circuit, main circuit main
module main (
  input  [7:0] bus_datain,
  input  load_in,
  input  rst,
  input  clk,
  output [7:0] contents,
  output [3:0] _4bit_data_out
);

  wire [7:0] controlled_buffer_1_out;

  assign controlled_buffer_1_out = load_in ? bus_datain : 8'bz;  // Controlled_Buffer controlled_buffer_1
  _8bit_reg_module_74_based_main main_1 (
    .internal_content({contents[7:4], _4bit_data_out}), .datain(controlled_buffer_1_out), .loadn(1'b0),
    .clk(clk), .rst(rst), .oe(1'b1));  // open: bus

  assign contents[3:0] = _4bit_data_out;
endmodule
