// Logisim project PC module logi based.circ as structural Verilog: 1 circuit, main circuit main
module main (
  input  nload,
  input  [7:0] data_in,
  input  clk,
  input  counten,
  input  rst,
  input  oen,
  output [7:0] contents,
  output Overflow,
  output [7:0] bus
);

  wire controlled_buffer_2_out, not_1_out, not_2_out, not_3_out;
  wire [7:0] controlled_buffer_1_out;

  assign controlled_buffer_1_out = not_1_out ? data_in : 8'bz;  // Controlled_Buffer controlled_buffer_1
  not not_1 (not_1_out, nload);
  not not_2 (not_2_out, nload);
  assign controlled_buffer_2_out = counten ? clk : 1'bz;  // Controlled_Buffer controlled_buffer_2
  assign controlled_buffer_1_out = not_3_out ? bus : 8'bz;  // Controlled_Buffer controlled_buffer_3
  not not_3 (not_3_out, oen);
  Counter #(.width(4), .max('hf)) counter_1 (
    .load(not_2_out), .D(controlled_buffer_1_out[3:0]), .count(nload), .Q(contents[3:0]), .carry(Overflow),
    .clk(controlled_buffer_2_out), .clr(rst));
  assign bus[3:0] = oen ? contents[3:0] : 4'bz;  // Controlled_Buffer controlled_buffer_4
  assign bus[7:4] = oen ? 4'b0000 : 4'bz;  // Controlled_Buffer controlled_buffer_5

  assign contents[7:4] = 4'b0000;

  // Notes on the sheet:
  //   nload: pull=up
  //   Load = load the data in to counter and wait
  //   count en = to count up continously, load must be disabled
endmodule
