// Logisim project PC module.circ as structural Verilog: 1 circuit, main circuit main
module main (
  input  load_en,
  input  [7:0] data_in,
  input  mode,
  input  OEN,
  input  clk,
  input  count_en,
  input  rst,
  output [7:0] contents,
  output Overflow,
  output [7:0] bus
);

  wire clock_1_out, controlled_buffer_1_out;

  Clock clock_1 (.out(clock_1_out));
  assign controlled_buffer_1_out = count_en ? clock_1_out : 1'bz;  // Controlled_Buffer controlled_buffer_1
  Counter #(.width(4), .max('hf)) counter_1 (
    .load(load_en), .D(data_in[3:0]), .count(mode), .Q(contents[3:0]), .carry(Overflow),
    .clk(controlled_buffer_1_out), .clr(rst));
  assign bus[3:0] = OEN ? contents[3:0] : 4'bz;  // Controlled_Buffer controlled_buffer_2
  assign bus[7:4] = OEN ? 4'b0000 : 4'bz;  // Controlled_Buffer controlled_buffer_3

  assign contents[7:4] = 4'b0000;
endmodule
