// Logisim project TEST PC.circ as structural Verilog: 1 circuit, main circuit main
module main (
  input  [3:0] in_1,
  input  in_2,
  input  in_3,
  input  in_4,
  output [3:0] out_5
);

  wire clock_1_out;

  Clock clock_1 (.out(clock_1_out));
  _4bit_counter_74_based_main main_1 (
    .nCLR(in_2), .nload(in_3), .ENT(in_4), .ENP(in_4), .clk(clock_1_out), .A(in_1[0]), .B(in_1[1]),
    .C(in_1[2]), .D(in_1[3]), .QA(out_5[0]), .QB(out_5[1]), .QC(out_5[2]), .QD(out_5[3]));  // open: RCO
endmodule
