// Logisim project display.circ as structural Verilog: 1 circuit, main circuit main
module main (
  input  loadn,
  input  [7:0] bus,
  input  rst,
  input  clk,
  input  MODE,
  output [7:0] SEG3,
  output [3:0] TOP_S3,
  output [3:0] BOTTOM_S3,
  output [7:0] SEG2,
  output [7:0] SEG1,
  output [3:0] TOP_S2,
  output [3:0] BOTTOM_S2,
  output [23:0] STATUS,
  output [3:0] TOP_S1,
  output [3:0] BOTTOM_S1,
  output SIGN_S0
);

  wire not_1_out, not_4_out;
  wire [6:0] controlled_buffer_1_out;
  wire [7:0] controlled_buffer_2_out, main_1_internal_content;
  wire [23:0] not_2_out, not_3_out, rom_1_data, rom_2_data;

  _7_Segment_Display u_7_segment_display_1 (
    .g(SEG1[0]), .f(SEG1[1]), .a(SEG1[6]), .b(SEG1[5]), .e(BOTTOM_S1[3]), .d(BOTTOM_S1[2]), .c(BOTTOM_S1[1]),
    .dp(BOTTOM_S1[0]));
  _7_Segment_Display u_7_segment_display_2 (.g(SIGN_S0));  // open: f, a, b, e, d, c, dp
  _7_Segment_Display u_7_segment_display_3 (
    .g(SEG3[0]), .f(SEG3[1]), .a(SEG3[6]), .b(SEG3[5]), .e(BOTTOM_S3[3]), .d(BOTTOM_S3[2]), .c(BOTTOM_S3[1]),
    .dp(BOTTOM_S3[0]));
  _7_Segment_Display u_7_segment_display_4 (
    .g(SEG2[0]), .f(SEG2[1]), .a(SEG2[6]), .b(SEG2[5]), .e(BOTTOM_S2[3]), .d(BOTTOM_S2[2]), .c(BOTTOM_S2[1]),
    .dp(BOTTOM_S2[0]));
  _8bit_reg_module_74_based_main main_1 (
    .internal_content(main_1_internal_content), .datain(bus), .loadn(loadn), .clk(clk), .rst(rst), .oe(1'b0));  // open: bus
  // Probe on main_1_internal_content
  not not_1 (not_1_out, MODE);
  assign {SIGN_S0, controlled_buffer_1_out} = MODE ? main_1_internal_content : 8'bz;  // Controlled_Buffer controlled_buffer_1
  assign controlled_buffer_2_out = not_1_out ? main_1_internal_content : 8'bz;  // Controlled_Buffer controlled_buffer_2
  ROM #(.dataWidth(24)) rom_1 (.addr(controlled_buffer_2_out), .data(rom_1_data));  // open: sel
  assign STATUS = not_1_out ? rom_1_data : 24'bz;  // Controlled_Buffer controlled_buffer_3
  assign STATUS = MODE ? rom_2_data : 24'bz;  // Controlled_Buffer controlled_buffer_4
  ROM #(.dataWidth(24)) rom_2 (.addr({SIGN_S0, controlled_buffer_1_out}), .data(rom_2_data));  // open: sel
  assign not_2_out = ~rom_1_data;  // NOT_Gate not_2, 24 bits wide
  assign not_3_out = ~rom_2_data;  // NOT_Gate not_3, 24 bits wide
  assign {SEG3[7:5], BOTTOM_S3[1], BOTTOM_S3[2], BOTTOM_S3[3], SEG3[1:0]} = not_4_out ? not_2_out[7:0] : 8'bz;  // Controlled_Buffer controlled_buffer_5
  assign {SEG2[7:5], BOTTOM_S2[1], BOTTOM_S2[2], BOTTOM_S2[3], SEG2[1:0]} = not_4_out ? not_2_out[15:8] : 8'bz;  // Controlled_Buffer controlled_buffer_6
  assign {SEG1[7:5], BOTTOM_S1[1], BOTTOM_S1[2], BOTTOM_S1[3], SEG1[1:0]} = not_4_out ? not_2_out[23:16] : 8'bz;  // Controlled_Buffer controlled_buffer_7
  not not_4 (not_4_out, MODE);
  assign {SEG3[7:5], BOTTOM_S3[1], BOTTOM_S3[2], BOTTOM_S3[3], SEG3[1:0]} = MODE ? not_3_out[7:0] : 8'bz;  // Controlled_Buffer controlled_buffer_8
  assign {SEG2[7:5], BOTTOM_S2[1], BOTTOM_S2[2], BOTTOM_S2[3], SEG2[1:0]} = MODE ? not_3_out[15:8] : 8'bz;  // Controlled_Buffer controlled_buffer_9
  assign {SEG1[7:5], BOTTOM_S1[1], BOTTOM_S1[2], BOTTOM_S1[3], SEG1[1:0]} = MODE ? not_3_out[23:16] : 8'bz;  // Controlled_Buffer controlled_buffer_10

  assign SEG1[4:2] = {BOTTOM_S1[1], BOTTOM_S1[2], BOTTOM_S1[3]};
  assign SEG2[4:2] = {BOTTOM_S2[1], BOTTOM_S2[2], BOTTOM_S2[3]};
  assign SEG3[4:2] = {BOTTOM_S3[1], BOTTOM_S3[2], BOTTOM_S3[3]};
  assign TOP_S1 = {SEG1[0], SEG1[1], SEG1[6:5]};
  assign TOP_S2 = {SEG2[0], SEG2[1], SEG2[6:5]};
  assign TOP_S3 = {SEG3[0], SEG3[1], SEG3[6:5]};

  // Other names for the same wires on the sheet: BS1[3:0] = BOTTOM_S1; BS2[3:0] = BOTTOM_S2; BS3[3:0] = BOTTOM_S3;
  //   TS1[3:0] = {SEG1[0], SEG1[1], SEG1[6:5]}; TS2[3:0] = {SEG2[0], SEG2[1], SEG2[6:5]};
  //   TS3[3:0] = {SEG3[0], SEG3[1], SEG3[6:5]}

  // Notes on the sheet:
  //   sin/unsin
  //   unsigned eeprom
  //   signed eeprom
  //   contents of rom_1 (hex, n*v repeats v):
  //   10101 4fffff 12ffff 6ffff 4cffff 24ffff 20ffff fffff ffff 4ffff 4f01ff 4f4fff 4f12ff 4f06ff 4f4cff
  //   4f24ff 4f20ff 4f0fff 4f00ff 4f04ff 1201ff 124fff 1212ff 1206ff 124cff 1224ff 1220ff 120fff 1200ff
  //   1204ff 601ff 64fff 612ff 606ff 64cff 624ff 620ff 60fff 600ff 604ff 4c01ff 4c4fff 4c12ff 4c06ff
  //   4c4cff 4c24ff 4c20ff 4c0fff 4c00ff 4c04ff 2401ff 244fff 2412ff 2406ff 244cff 2424ff 2420ff 240fff
  //   2400ff 2404ff 2001ff 204fff 2012ff 2006ff 204cff 2024ff 2020ff 200fff 2000ff 2004ff f01ff f4fff
  //   f12ff f06ff f4cff f24ff f20ff f0fff f00ff f04ff 1ff 4fff 12ff 6ff 4cff 24ff 20ff fff ff 4ff 401ff
  //   44fff 412ff 406ff 44cff 424ff 420ff 40fff 400ff 404ff 4f0101 4f014f 4f0112 4f0106 4f014c 4f0124
  //   4f0120 4f010f 4f0100 4f0104 4f4f01 4f4f4f 4f4f12 4f4f06 4f4f4c 4f4f24 4f4f20 4f4f0f 4f4f00 4f4f04
  //   4f1201 4f124f 4f1212 4f1206 4f124c 4f1224 4f1220 4f120f 4f1200 4f1204 4f0601 4f064f 4f0612 4f0606
  //   4f064c 4f0624 4f0620 4f060f 4f0600 4f0604 4f4c01 4f4c4f 4f4c12 4f4c06 4f4c4c 4f4c24 4f4c20 4f4c0f
  //   4f4c00 4f4c04 4f2401 4f244f 4f2412 4f2406 4f244c 4f2424 4f2420 4f240f 4f2400 4f2404 4f2001 4f204f
  //   4f2012 4f2006 4f204c 4f2024 4f2020 4f200f 4f2000 4f2004 4f0f01 4f0f4f 4f0f12 4f0f06 4f0f4c 4f0f24
  //   4f0f20 4f0f0f 4f0f00 4f0f04 4f0001 4f004f 4f0012 4f0006 4f004c 4f0024 4f0020 4f000f 4f0000 4f0004
  //   4f0401 4f044f 4f0412 4f0406 4f044c 4f0424 4f0420 4f040f 4f0400 4f0404 120101 12014f 120112 120106
  //   12014c 120124 120120 12010f 120100 120104 124f01 124f4f 124f12 124f06 124f4c 124f24 124f20 124f0f
  //   124f00 124f04 121201 12124f 121212 121206 12124c 121224 121220 12120f 121200 121204 120601 12064f
  //   120612 120606 12064c 120624 120620 12060f 120600 120604 124c01 124c4f 124c12 124c06 124c4c 124c24
  //   124c20 124c0f 124c00 124c04 122401 12244f 122412 122406 12244c 122424
  //   contents of rom_2 (hex, n*v repeats v):
  //   10101 4fffff 12ffff 6ffff 4cffff 24ffff 20ffff fffff ffff 4ffff 4f01ff 4f4fff 4f12ff 4f06ff 4f4cff
  //   4f24ff 4f20ff 4f0fff 4f00ff 4f04ff 1201ff 124fff 1212ff 1206ff 124cff 1224ff 1220ff 120fff 1200ff
  //   1204ff 601ff 64fff 612ff 606ff 64cff 624ff 620ff 60fff 600ff 604ff 4c01ff 4c4fff 4c12ff 4c06ff
  //   4c4cff 4c24ff 4c20ff 4c0fff 4c00ff 4c04ff 2401ff 244fff 2412ff 2406ff 244cff 2424ff 2420ff 240fff
  //   2400ff 2404ff 2001ff 204fff 2012ff 2006ff 204cff 2024ff 2020ff 200fff 2000ff 2004ff f01ff f4fff
  //   f12ff f06ff f4cff f24ff f20ff f0fff f00ff f04ff 1ff 4fff 12ff 6ff 4cff 24ff 20ff fff ff 4ff 401ff
  //   44fff 412ff 406ff 44cff 424ff 420ff 40fff 400ff 404ff 4f0101 4f014f 4f0112 4f0106 4f014c 4f0124
  //   4f0120 4f010f 4f0100 4f0104 4f4f01 4f4f4f 4f4f12 4f4f06 4f4f4c 4f4f24 4f4f20 4f4f0f 4f4f00 4f4f04
  //   4f1201 4f124f 4f1212 4f1206 4f124c 4f1224 4f1220 4f120f 4f1200 4f120f 4f1220 4f1224 4f124c 4f1206
  //   4f1212 4f124f 4f1201 4f4f04 4f4f00 4f4f0f 4f4f20 4f4f24 4f4f4c 4f4f06 4f4f12 4f4f4f 4f4f01 4f0104
  //   4f0100 4f010f 4f0120 4f0124 4f014c 4f0106 4f0112 4f014f 4f0101 404ff 400ff 40fff 420ff 424ff 44cff
  //   406ff 412ff 44fff 401ff 4ff ff fff 20ff 24ff 4cff 6ff 12ff 4fff 1ff f04ff f00ff f0fff f20ff f24ff
  //   f4cff f06ff f12ff f4fff f01ff 2004ff 2000ff 200fff 2020ff 2024ff 204cff 2006ff 2012ff 204fff 2001ff
  //   2404ff 2400ff 240fff 2420ff 2424ff 244cff 2406ff 2412ff 244fff 2401ff 4c04ff 4c00ff 4c0fff 4c20ff
  //   4c24ff 4c4cff 4c06ff 4c12ff 4c4fff 4c01ff 604ff 600ff 60fff 620ff 624ff 64cff 606ff 612ff 64fff
  //   601ff 1204ff 1200ff 120fff 1220ff 1224ff 124cff 1206ff 1212ff 124fff 1201ff 4f04ff 4f00ff 4f0fff
  //   4f20ff 4f24ff 4f4cff 4f06ff 4f12ff 4f4fff 4f01ff 4ffff ffff fffff 20ffff 24ffff 4cffff 6ffff 12ffff
  //   4fffff
endmodule
