// Logisim project fetch cycle tracker.circ as structural Verilog: 1 circuit, main circuit main
module main (
  input  nclk,
  output [2:0] STATUS,
  output [2:0] STEP_LINE
);

  wire and_1_out, nand_4_out, nand_5_out, nand_6_out, nand_7_out, nand_8_out, not_1_out, not_2_out,
       not_3_out, not_4_out, not_5_out, not_6_out, not_7_out, not_8_out, not_9_out, not_10_out, not_11_out,
       not_12_out;
  wire [2:0] nand_1_out;

  Counter #(.width(3), .max('h7)) counter_1 (
    .load(1'b0), .count(1'b1), .Q(STATUS), .clk(not_1_out), .clr(not_12_out));  // open: D, carry
  not not_1 (not_1_out, nclk);
  not not_2 (not_2_out, 1'b1);
  not not_3 (not_3_out, not_2_out);
  not not_4 (not_4_out, 1'b0);
  and and_1 (and_1_out, not_3_out, not_4_out, not_5_out);
  not not_5 (not_5_out, 1'b0);
  not not_6 (not_6_out, STATUS[0]);
  not not_7 (not_7_out, STATUS[1]);
  not not_8 (not_8_out, STATUS[2]);
  not not_9 (not_9_out, not_6_out);
  not not_10 (not_10_out, not_7_out);
  not not_11 (not_11_out, not_8_out);
  nand nand_1 (nand_1_out[0], not_6_out, not_7_out, not_8_out, and_1_out);
  nand nand_2 (nand_1_out[1], not_9_out, not_7_out, not_8_out, and_1_out);
  nand nand_3 (nand_1_out[2], not_6_out, not_10_out, not_8_out, and_1_out);
  nand nand_4 (nand_4_out, not_9_out, not_10_out, not_8_out, and_1_out);
  nand nand_5 (nand_5_out, not_6_out, not_7_out, not_11_out, and_1_out);
  nand nand_6 (nand_6_out, not_7_out, not_11_out, not_9_out, and_1_out);
  nand nand_7 (nand_7_out, not_6_out, not_11_out, not_10_out, and_1_out);
  nand nand_8 (nand_8_out, and_1_out, not_10_out, not_9_out, not_11_out);
  // Probe on nand_1_out[0]
  // Probe on nand_1_out[1]
  // Probe on nand_1_out[2]
  // Probe on nand_4_out
  // Probe on nand_5_out
  // Probe on nand_6_out
  // Probe on nand_7_out
  // Probe on nand_8_out
  not not_12 (not_12_out, nand_6_out);
  assign STEP_LINE = ~nand_1_out;  // NOT_Gate not_13, 3 bits wide

  // Notes on the sheet:
  //   TRACKS MAX STEPS REQUIRED TO PERFOEM A INSCTUCTION FETCH
  //   lesser the steps, faster the cpu executes the data math 
  //   T0-T3
  //   4 STEPS
  //   000
  //   001
  //   010
  //   100
  //   000
  //   MICRO INSTRUCTION EXECUTUIONCOUNTER
endmodule
