// Logisim project ff.circ as structural Verilog: 1 circuit, main circuit main
module main (
  input  nR,
  input  TE,
  input  nclk,
  input  D,
  input  Load,
  output Q1,
  output Q2
);

  wire and_1_out, and_2_out, and_3_out, and_4_out, clock_1_out, nand_1_out, nand_2_out, nand_3_out,
       nand_4_out, nand_5_out, nand_6_out, not_1_out, not_2_out, xnor_1_out, xnor_2_out;

  Clock clock_1 (.out(clock_1_out));
  xnor xnor_1 (xnor_1_out, nand_6_out, TE);
  xnor xnor_2 (xnor_2_out, TE, nand_5_out);
  nand nand_1 (nand_1_out, D, Load);
  and and_1 (and_1_out, xnor_1_out, nand_4_out);
  and and_2 (and_2_out, and_1_out, nand_1_out);
  and and_3 (and_3_out, nand_3_out, xnor_2_out);
  nand nand_2 (nand_2_out, nand_1_out, Load);
  and and_4 (and_4_out, nR, and_3_out, nand_2_out);
  not not_1 (not_1_out, clock_1_out);
  not not_2 (not_2_out, clock_1_out);
  nand nand_3 (nand_3_out, and_2_out, not_1_out);
  nand nand_4 (nand_4_out, not_2_out, and_4_out);
  nand nand_5 (nand_5_out, nand_3_out, nR, nand_6_out);
  nand nand_6 (nand_6_out, nand_5_out, nand_4_out);
  nand nand_7 (Q1, nand_5_out, nand_4_out);
  nand nand_8 (Q2, nand_5_out, nand_4_out);
endmodule
