// Logisim project instruction register module.circ as structural Verilog: 1 circuit, main circuit main
module main (
  input  [7:0] Datain,
  input  loadin,
  input  clk,
  input  rst,
  input  oen,
  output [7:0] Bus,
  output [3:0] MSB_ST,
  output [3:0] LSB_ST,
  output [3:0] Instr_nibble
);

  wire not_1_out, not_2_out;
  wire [7:0] controlled_buffer_1_out, main_1_bus;
  wire [7:4] controlled_buffer_3_out;

  assign controlled_buffer_1_out = not_1_out ? Datain : 8'bz;  // Controlled_Buffer controlled_buffer_1
  not not_1 (not_1_out, loadin);
  assign controlled_buffer_1_out = not_2_out ? {controlled_buffer_3_out, Bus[3:0]} : 8'bz;  // Controlled_Buffer controlled_buffer_2
  not not_2 (not_2_out, oen);
  _8bit_reg_module_74_based_main main_1 (
    .internal_content({Instr_nibble, LSB_ST}), .datain(controlled_buffer_1_out), .loadn(loadin), .clk(clk),
    .rst(rst), .oe(oen), .bus(main_1_bus));
  assign {controlled_buffer_3_out, Bus[3:0]} = oen ? main_1_bus : 8'bz;  // Controlled_Buffer controlled_buffer_3
  assign Bus[7:4] = oen ? 4'b0000 : 4'bz;  // Controlled_Buffer controlled_buffer_4

  assign MSB_ST = Instr_nibble;

  // Notes on the sheet:
  //   loadin: pull=up
endmodule
