// Logisim project ram module without MAR.circ as structural Verilog: 1 circuit, main circuit main
module main (
  input  [7:0] data_in,
  input  [3:0] add_in,
  input  clr,
  input  clk,
  input  write,
  input  oe,
  output [7:0] contents,
  output [7:0] bus
);

  wire not_1_out;

  assign contents = write ? data_in : 8'bz;  // Controlled_Buffer controlled_buffer_1
  not not_1 (not_1_out, write);
  ROM #(.addrWidth(4)) rom_1 (.addr(add_in), .data(contents), .sel(1'b1));
  assign bus = oe ? contents : 8'bz;  // Controlled_Buffer controlled_buffer_2

  // Notes on the sheet:
  //   contents of rom_1 (hex, n*v repeats v):
  //   1e 3f e0 11*0 1c e
endmodule
