// Logisim project ram module.circ as structural Verilog: 1 circuit, main circuit main
module main (
  input  [7:0] data_in,
  input  [7:0] add_in,
  input  ld,
  input  clr,
  input  clk,
  input  write,
  input  oe,
  output [7:0] contents,
  output [7:0] bus
);

  wire not_1_out;
  wire [7:0] controlled_buffer_1_out, main_1_internal_content;

  assign controlled_buffer_1_out = ld ? add_in : 8'bz;  // Controlled_Buffer controlled_buffer_1
  _8bit_reg_module_74_based_main main_1 (
    .internal_content(main_1_internal_content), .datain(controlled_buffer_1_out), .loadn(1'b0), .clk(clk),
    .rst(clr), .oe(1'b1));  // open: bus
  assign contents = write ? data_in : 8'bz;  // Controlled_Buffer controlled_buffer_2
  not not_1 (not_1_out, write);
  RAM #(.addrWidth(4)) ram_1 (
    .addr(main_1_internal_content[3:0]), .data(contents), .sel(1'b1), .clk(clk), .ld(not_1_out), .clr(clr));
  assign bus = oe ? contents : 8'bz;  // Controlled_Buffer controlled_buffer_3

  // Notes on the sheet:
  //   Memory Address Register
endmodule
