// Logisim project Program_counter.circ as structural Verilog: 1 circuit, main circuit main
module main (
  input  LOAD_EN,
  input  [7:0] DATA_IN,
  input  MODE,
  input  OEN,
  input  CLK,
  input  EN_COUNT,
  input  RST,
  output [7:0] STATUS,
  output OVERFLOW,
  output [7:0] OUT
);

  wire controlled_buffer_1_out;

  assign controlled_buffer_1_out = EN_COUNT ? CLK : 1'bz;  // Controlled_Buffer controlled_buffer_1
  Counter #(.width(4), .max('hf)) counter_1 (
    .load(LOAD_EN), .D(DATA_IN[3:0]), .count(MODE), .Q(STATUS[3:0]), .carry(OVERFLOW),
    .clk(controlled_buffer_1_out), .clr(RST));
  assign OUT[3:0] = OEN ? STATUS[3:0] : 4'bz;  // Controlled_Buffer controlled_buffer_2
  assign OUT[7:4] = OEN ? 4'b0000 : 4'bz;  // Controlled_Buffer controlled_buffer_3

  assign STATUS[7:4] = 4'b0000;

  // Notes on the sheet:
  //   data
endmodule
