// Logisim project RAMMODULE.circ as structural Verilog: 1 circuit, main circuit main
module main (
  input  [7:0] DATAIN,
  input  [7:0] ADDRESS,
  input  OEN,
  input  LOAD_ADDRES,
  input  WRITE,
  input  CLR,
  input  CLK,
  output [7:0] STATUS,
  output [7:0] OUTPUT
);

  wire not_1_out;
  wire [7:0] controlled_buffer_1_out, register_1_contents;

  assign controlled_buffer_1_out = LOAD_ADDRES ? ADDRESS : 8'bz;  // Controlled_Buffer controlled_buffer_1
  register register_1 (
    .INPUT(controlled_buffer_1_out), .LOAD(1'b1), .RESET(CLR), .CONTENTS(register_1_contents), .ENABLE(1'b0),
    .CLOCK(CLK));  // open: OUTPUT
  assign STATUS = WRITE ? DATAIN : 8'bz;  // Controlled_Buffer controlled_buffer_2
  not not_1 (not_1_out, WRITE);
  RAM #(.addrWidth(4)) ram_1 (
    .addr(register_1_contents[3:0]), .data(STATUS), .sel(1'b1), .clk(CLK), .ld(not_1_out), .clr(CLR));
  assign OUTPUT = OEN ? STATUS : 8'bz;  // Controlled_Buffer controlled_buffer_3
endmodule
