// Logisim project THE COMPUTER ITSELF.circ as structural Verilog: 1 circuit, main circuit main
module main (
  input  in_1,
  input  in_2,
  input  in_3,
  input  in_4,
  input  [7:0] in_5,
  input  [7:0] in_6,
  input  in_7,
  input  in_8,
  output [7:0] BUS,
  output [7:0] out_10,
  output [7:0] out_11,
  output out_12,
  output [7:0] out_13,
  output [3:0] out_14,
  output [3:0] out_15,
  output [7:0] out_16,
  output [3:0] out_17,
  output out_18,
  output [2:0] out_19,
  output [7:0] out_20,
  output [7:0] out_21,
  output [23:0] out_22
);

  wire clock_1_out, clock_halt_1_clkout, DISP_sign, not_1_out, PC_overflow;
  wire [3:0] n7decoder_1_bottom, n7decoder_1_top, n7decoder_2_bottom, n7decoder_2_top, n7decoder_3_bottom,
       n7decoder_3_top;
  wire [7:0] DISP_seg1, DISP_seg2, DISP_seg3;
  wire [14:0] controlled_buffer_1_out, rom_1_data;

  Clock clock_1 (.out(clock_1_out));
  assign controlled_buffer_1_out = in_8 ? {in_5, in_6[6:0]} : 15'bz;  // Controlled_Buffer controlled_buffer_1
  clock_halt clock_halt_1 (.CLKIN(clock_1_out), .HLT(controlled_buffer_1_out[14]), .CLKOUT(clock_halt_1_clkout));
  not not_1 (not_1_out, in_8);
  assign controlled_buffer_1_out = not_1_out ? rom_1_data : 15'bz;  // Controlled_Buffer controlled_buffer_2
  RAMMODULE_main RAM (
    .DATAIN(BUS), .OEN(controlled_buffer_1_out[11]), .WRITE(controlled_buffer_1_out[12]), .CLR(in_3),
    .STATUS(out_11), .OUTPUT(BUS), .CLK(clock_halt_1_clkout), .ADDRESS(BUS),
    .LOAD_ADDRES(controlled_buffer_1_out[13]));
  ROM #(.addrWidth(7), .dataWidth(15)) rom_1 (.addr({out_17, out_19}), .data(rom_1_data));  // open: sel
  instruction_register_main IR (
    .DATA_IN(BUS), .LOAD(controlled_buffer_1_out[9]), .CLK(clock_halt_1_clkout), .RST(in_3),
    .OEN(controlled_buffer_1_out[10]), ._4BL_OUT(BUS), .MSB_ST(out_14), .LSB_ST(out_15), .INST_DECO(out_17));
  instruction_decoder_main IR_DEC (.CLK(clock_halt_1_clkout), .STATUS(out_19), .STEP_LINE(out_20));
  Program_counter_main PC (
    .LOAD_EN(in_2), .DATA_IN(BUS), .MODE(in_1), .OEN(controlled_buffer_1_out[1]),
    .EN_COUNT(controlled_buffer_1_out[2]), .RST(in_3), .OVERFLOW(PC_overflow), .OUT(BUS), .STATUS(out_10),
    .CLK(clock_halt_1_clkout));
  register A_REG (
    .INPUT(BUS), .OUTPUT(BUS), .LOAD(controlled_buffer_1_out[8]), .RESET(in_3), .STATUS(out_13),
    .ENABLE(controlled_buffer_1_out[7]), .CLOCK(clock_halt_1_clkout));
  alu ALU (
    .status(out_16), .OUTPUT(BUS), .SUB(controlled_buffer_1_out[5]), .ACC(out_13), .B_reg(out_21),
    .C_OUT(out_18), .enable(controlled_buffer_1_out[6]));
  register B_REG (
    .INPUT(BUS), .OUTPUT(BUS), .LOAD(controlled_buffer_1_out[4]), .RESET(in_3), .STATUS(out_21),
    .ENABLE(in_4), .CLOCK(clock_halt_1_clkout));
  EEPROM_DECODER DISP (
    .INPUT(BUS), .MODE(in_7), .SEG1(DISP_seg1), .SEG2(DISP_seg2), .SEG3(DISP_seg3), .SIGN(DISP_sign),
    .STATUS(out_22), .LOAD(controlled_buffer_1_out[3]), .RESET(in_3), .CLK(clock_halt_1_clkout));
  _7decoder u_7decoder_1 (.INPUT(DISP_seg1), .TOP(n7decoder_1_top), .BOTTOM(n7decoder_1_bottom));
  _7decoder u_7decoder_2 (.INPUT(DISP_seg2), .TOP(n7decoder_2_top), .BOTTOM(n7decoder_2_bottom));
  _7decoder u_7decoder_3 (.INPUT(DISP_seg3), .TOP(n7decoder_3_top), .BOTTOM(n7decoder_3_bottom));
  _7_Segment_Display u_7_segment_display_1 (.g(DISP_sign));  // open: f, a, b, e, d, c, dp
  _7_Segment_Display u_7_segment_display_2 (
    .g(n7decoder_1_top[3]), .f(n7decoder_1_top[2]), .a(n7decoder_1_top[1]), .b(n7decoder_1_top[0]),
    .e(n7decoder_1_bottom[3]), .d(n7decoder_1_bottom[2]), .c(n7decoder_1_bottom[1]),
    .dp(n7decoder_1_bottom[0]));
  _7_Segment_Display u_7_segment_display_3 (
    .g(n7decoder_3_top[3]), .f(n7decoder_3_top[2]), .a(n7decoder_3_top[1]), .b(n7decoder_3_top[0]),
    .e(n7decoder_3_bottom[3]), .d(n7decoder_3_bottom[2]), .c(n7decoder_3_bottom[1]),
    .dp(n7decoder_3_bottom[0]));
  _7_Segment_Display u_7_segment_display_4 (
    .g(n7decoder_2_top[3]), .f(n7decoder_2_top[2]), .a(n7decoder_2_top[1]), .b(n7decoder_2_top[0]),
    .e(n7decoder_2_bottom[3]), .d(n7decoder_2_bottom[2]), .c(n7decoder_2_bottom[1]),
    .dp(n7decoder_2_bottom[0]));

  assign in_6[7] = in_5[0];

  // Notes on the sheet:
  //   contents of rom_1 (hex, n*v repeats v):
  //   0 0 2002
endmodule
