// Logisim project clock unit.circ as structural Verilog: 1 circuit, main circuit clock halt
module clock_halt (
  input  CLKIN,
  input  HLT,
  output CLKOUT
);

  wire not_1_out;

  not not_1 (not_1_out, HLT);
  and and_1 (CLKOUT, CLKIN, not_1_out);
endmodule
