// Logisim project hexa test.circ as structural Verilog: 1 circuit, main circuit hex
module hex (
  input  [7:0] in_1,
  output [6:0] out_2
);

  wire [6:0] not_1_out;

  ROM #(.dataWidth(7)) rom_1 (.addr(in_1), .data(out_2));  // open: sel
  assign not_1_out = ~out_2;  // NOT_Gate not_1, 7 bits wide
  _7_Segment_Display u_7_segment_display_1 (
    .g(not_1_out[0]), .f(not_1_out[1]), .a(not_1_out[6]), .b(not_1_out[5]), .e(not_1_out[2]),
    .d(not_1_out[3]), .c(not_1_out[4]));  // open: dp

  // Notes on the sheet:
  //   contents of rom_1 (hex, n*v repeats v):
  //   1 4f 12 6 4c 24 20 f 0 4 8 60 31 42 30 38
endmodule
