// Logisim project instruction decoder.circ as structural Verilog: 1 circuit, main circuit main
module main (
  input  CLK,
  output [2:0] STATUS,
  output [7:0] STEP_LINE
);

  wire not_1_out;

  Counter #(.width(3), .max('h7)) counter_1 (
    .load(1'b0), .count(1'b1), .Q(STATUS), .clk(not_1_out), .clr(STEP_LINE[5]));  // open: D, carry
  not not_1 (not_1_out, CLK);
  Demultiplexer #(.select(3)) demultiplexer_1 (
    .out0(STEP_LINE[0]), .out1(STEP_LINE[1]), .out2(STEP_LINE[2]), .out3(STEP_LINE[3]), .out4(STEP_LINE[4]),
    .out5(STEP_LINE[5]), .out6(STEP_LINE[6]), .out7(STEP_LINE[7]), .in(1'b1), .sel(STATUS));  // open: en
endmodule
